// Logisim project UAL.circ as structural Verilog: 5 circuits, main circuit main
module main (
);

  wire clock_1_out, decodeur_instruction_1_isload, decodeur_instruction_1_out_3,
       decodeur_instruction_1_regwrite, Reset_out;
  wire [1:0] controle_de_saut_1_out_3;
  wire [2:0] decodeur_instruction_1_out_4;
  wire [3:0] selecteurreg_1_rd, selecteurreg_1_rs, selecteurreg_1_rt_2, ual_1_flags;
  wire [7:0] adder_1_out, adder_2_out, bancderegistres_1_out_8, bancderegistres_1_rs, bit_extender_1_out,
       multiplexer_1_out, multiplexer_2_out, register_1_q, ual_1_out_5;
  wire [15:0] rom_1_data;

  Button Reset (.out(Reset_out));
  Clock clock_1 (.out(clock_1_out));
  Register register_1 (.D(multiplexer_2_out), .en(1'b1), .Q(register_1_q), .clk(clock_1_out), .clr(Reset_out));
  Adder adder_1 (.a(register_1_q), .b(8'h1), .out(adder_1_out));  // open: cin, cout
  ROM #(.dataWidth(16)) rom_1 (.addr(register_1_q), .data(rom_1_data));  // open: sel
  SelecteurReg selecteurreg_1 (
    .IsJMP(decodeur_instruction_1_out_3), .rd_rs(rom_1_data[11:8]), .rs_rt(rom_1_data[7:4]),
    .rt(rom_1_data[3:0]), .rd(selecteurreg_1_rd), .rs(selecteurreg_1_rs), .rt_2(selecteurreg_1_rt_2));
  Multiplexer #(.width(8)) multiplexer_1 (
    .in0(ual_1_out_5), .in1(rom_1_data[7:0]), .out(multiplexer_1_out), .sel(decodeur_instruction_1_isload));  // open: en
  decodeur_instruction decodeur_instruction_1 (
    .regWrite(decodeur_instruction_1_regwrite), .out_3(decodeur_instruction_1_out_3),
    .isLoad(decodeur_instruction_1_isload), .in_1(rom_1_data[15:12]), .out_4(decodeur_instruction_1_out_4));
  BancDeRegistres bancderegistres_1 (
    .Reset(Reset_out), .InputClock(clock_1_out), .regW(decodeur_instruction_1_regwrite),
    .Rs(bancderegistres_1_rs), .Selec_rd(selecteurreg_1_rd), .Selc_rt(selecteurreg_1_rt_2),
    .Selec_rs(selecteurreg_1_rs), .ValIn(multiplexer_1_out), .out_8(bancderegistres_1_out_8));
  assign bit_extender_1_out = {{4{rom_1_data[3]}}, rom_1_data[3:0]};  // Bit_Extender bit_extender_1
  Adder adder_2 (.a(adder_1_out), .b(bit_extender_1_out), .out(adder_2_out));  // open: cin, cout
  UAL ual_1 (
    .in_3(decodeur_instruction_1_out_4), .Flags(ual_1_flags), .out_5(ual_1_out_5), .rs(bancderegistres_1_rs),
    .rt(bancderegistres_1_out_8));
  Multiplexer #(.select(2), .width(8)) multiplexer_2 (
    .in1(adder_2_out), .in2(adder_1_out), .in3({8{1'b1}}), .out(multiplexer_2_out),
    .sel(controle_de_saut_1_out_3));  // open: in0, en
  controle_de_saut controle_de_saut_1 (
    .OF_SF_ZF_CF(ual_1_flags), .opcode(rom_1_data[15:12]), .out_3(controle_de_saut_1_out_3));

  // Notes on the sheet:
  //   contents of rom_1 (hex, n*v repeats v):
  //   f010 f102 9014 c011 2001 2110 800b
endmodule

module UAL (
  input  [7:0] rs,
  input  [7:0] rt,
  input  [2:0] in_3,
  output [3:0] Flags,
  output [7:0] out_5
);

  wire adder_1_cout, and_1_out, and_2_out, and_4_out, and_5_out, and_6_out, and_7_out, and_8_out, and_9_out,
       and_10_out, and_11_out, and_12_out, or_2_out, or_3_out, subtractor_1_bout;
  wire [7:0] adder_1_out, and_3_out, not_1_out, or_1_out, shifter_1_out, shifter_2_out, subtractor_1_out;

  and and_1 (and_1_out, ~rs[7], ~rt[7]);  // AND_Gate
  and and_2 (and_2_out, rs[7], rt[7]);
  Adder adder_1 (.a(rs), .b(rt), .out(adder_1_out), .cout(adder_1_cout));  // open: cin
  Subtractor subtractor_1 (.a(rs), .b(rt), .out(subtractor_1_out), .bout(subtractor_1_bout));  // open: bin
  assign or_1_out = rs | rt;  // OR_Gate or_1, 8 bits wide
  assign and_3_out = rs & rt;  // AND_Gate and_3, 8 bits wide
  assign not_1_out = ~rs;  // NOT_Gate not_1, 8 bits wide
  Shifter shifter_1 (.in(rs), .\dist (rt[2:0]), .out(shifter_1_out));
  Shifter #(.shift("lr")) shifter_2 (.in(rs), .\dist (rt[2:0]), .out(shifter_2_out));
  and and_4 (and_4_out, and_1_out, adder_1_out[7]);
  or or_2 (or_2_out, and_2_out, and_1_out);
  and and_5 (and_5_out, and_2_out, ~adder_1_out[7]);  // AND_Gate
  or or_3 (or_3_out, and_4_out, and_5_out);
  and and_6 (and_6_out, subtractor_1_out[0], or_2_out);
  and and_7 (and_7_out, and_6_out, and_10_out);
  Multiplexer #(.select(3), .width(8)) multiplexer_1 (
    .in0({8{1'b1}}), .in1(adder_1_out), .in2(subtractor_1_out), .in3(or_1_out), .in4(and_3_out),
    .in5(not_1_out), .in6(shifter_1_out), .in7(shifter_2_out), .out({Flags[2], out_5[6:0]}), .sel(in_3));  // open: en
  or or_4 (Flags[3], and_7_out, and_8_out);
  and and_8 (and_8_out, and_9_out, or_3_out);
  nor nor_1 (Flags[1], out_5[0], out_5[1], out_5[2], out_5[3], out_5[4], out_5[5], out_5[6], Flags[2]);
  and and_9 (and_9_out, in_3[0], ~in_3[1], ~in_3[2]);  // AND_Gate
  and and_10 (and_10_out, ~in_3[0], in_3[1], ~in_3[2]);  // AND_Gate
  or or_5 (Flags[0], and_11_out, and_12_out);
  and and_11 (and_11_out, adder_1_cout, and_9_out);
  and and_12 (and_12_out, subtractor_1_bout, and_10_out);

  assign out_5[7] = Flags[2];

  // Notes on the sheet:
  //   OF pour sub
  //   OF pour l'addition
  //   ZF
  //   halt
  //   Halt
  //   code add
  //   code sub
  //   OP code add
  //   OF
  //   SF
  //   CF add
  //   Of SF ZF CF
  //   CF sub
endmodule

module BancDeRegistres (
  input  [7:0] ValIn,
  input  Reset,
  input  [3:0] Selec_rd,
  input  [3:0] Selc_rt,
  input  InputClock,
  input  regW,
  input  [3:0] Selec_rs,
  output [7:0] out_8,
  output [7:0] Rs
);

  wire demultiplexer_1_out0, demultiplexer_1_out1, demultiplexer_1_out2, demultiplexer_1_out3,
       demultiplexer_1_out4, demultiplexer_1_out5, demultiplexer_1_out6, demultiplexer_1_out7,
       demultiplexer_1_out8, demultiplexer_1_out9, demultiplexer_1_out10, demultiplexer_1_out11,
       demultiplexer_1_out12, demultiplexer_1_out13, demultiplexer_1_out14, demultiplexer_1_out15;
  wire [7:0] R1, R2, R3, R4, R5, R6, R7, R8, R9, R10, R11, R12, R13, R14, R15, R16;

  Register u_r16 (.D(ValIn), .en(demultiplexer_1_out15), .Q(R16), .clk(InputClock), .clr(Reset));
  Register u_r14 (.D(ValIn), .en(demultiplexer_1_out13), .Q(R14), .clk(InputClock), .clr(Reset));
  Register u_r15 (.D(ValIn), .en(demultiplexer_1_out14), .Q(R15), .clk(InputClock), .clr(Reset));
  Register u_r13 (.D(ValIn), .en(demultiplexer_1_out12), .Q(R13), .clk(InputClock), .clr(Reset));
  Register u_r11 (.D(ValIn), .en(demultiplexer_1_out10), .Q(R11), .clk(InputClock), .clr(Reset));
  Register u_r12 (.D(ValIn), .en(demultiplexer_1_out11), .Q(R12), .clk(InputClock), .clr(Reset));
  Register u_r9 (.D(ValIn), .en(demultiplexer_1_out8), .Q(R9), .clk(InputClock), .clr(Reset));
  Register u_r10 (.D(ValIn), .en(demultiplexer_1_out9), .Q(R10), .clk(InputClock), .clr(Reset));
  Register u_r8 (.D(ValIn), .en(demultiplexer_1_out7), .Q(R8), .clk(InputClock), .clr(Reset));
  Register u_r6 (.D(ValIn), .en(demultiplexer_1_out5), .Q(R6), .clk(InputClock), .clr(Reset));
  Register u_r7 (.D(ValIn), .en(demultiplexer_1_out6), .Q(R7), .clk(InputClock), .clr(Reset));
  Register u_r5 (.D(ValIn), .en(demultiplexer_1_out4), .Q(R5), .clk(InputClock), .clr(Reset));
  Register u_r3 (.D(ValIn), .en(demultiplexer_1_out2), .Q(R3), .clk(InputClock), .clr(Reset));
  Register u_r4 (.D(ValIn), .en(demultiplexer_1_out3), .Q(R4), .clk(InputClock), .clr(Reset));
  Register u_r1 (.D(ValIn), .en(demultiplexer_1_out0), .Q(R1), .clk(InputClock), .clr(Reset));
  Register u_r2 (.D(ValIn), .en(demultiplexer_1_out1), .Q(R2), .clk(InputClock), .clr(Reset));
  Demultiplexer #(.select(4)) demultiplexer_1 (
    .out0(demultiplexer_1_out0), .out1(demultiplexer_1_out1), .out2(demultiplexer_1_out2),
    .out3(demultiplexer_1_out3), .out4(demultiplexer_1_out4), .out5(demultiplexer_1_out5),
    .out6(demultiplexer_1_out6), .out7(demultiplexer_1_out7), .out8(demultiplexer_1_out8),
    .out9(demultiplexer_1_out9), .out10(demultiplexer_1_out10), .out11(demultiplexer_1_out11),
    .out12(demultiplexer_1_out12), .out13(demultiplexer_1_out13), .out14(demultiplexer_1_out14),
    .out15(demultiplexer_1_out15), .in(regW), .sel(Selec_rd));  // open: en
  Multiplexer #(.select(4), .width(8)) multiplexer_1 (
    .in0(R1), .in1(R2), .in2(R3), .in3(R4), .in4(R5), .in5(R6), .in6(R7), .in7(R8), .in8(R9), .in9(R10),
    .in10(R11), .in11(R12), .in12(R13), .in13(R14), .in14(R15), .in15(R16), .out(out_8), .sel(Selc_rt));  // open: en
  Multiplexer #(.select(4), .width(8)) multiplexer_2 (
    .in0(R1), .in1(R2), .in2(R3), .in3(R4), .in4(R5), .in5(R6), .in6(R7), .in7(R8), .in8(R9), .in9(R10),
    .in10(R11), .in11(R12), .in12(R13), .in13(R14), .in14(R15), .in15(R16), .out(Rs), .sel(Selec_rs));  // open: en

  // Other names for the same wires on the sheet: rg = regW
endmodule

module SelecteurReg (
  input  [3:0] rd_rs,
  input  [3:0] rs_rt,
  input  [3:0] rt,
  input  IsJMP,
  output [3:0] rd,
  output [3:0] rs,
  output [3:0] rt_2
);

  Demultiplexer #(.width(4), .tristate("true")) demultiplexer_1 (
    .out0(rd), .out1(rs), .in(rd_rs), .sel(IsJMP));  // open: en
  Demultiplexer #(.width(4), .tristate("true")) demultiplexer_2 (
    .out0(rs), .out1(rt_2), .in(rs_rt), .sel(IsJMP));  // open: en
  Demultiplexer #(.width(4), .tristate("true")) demultiplexer_3 (
    .out0(rt_2), .out1(rd), .in(rt), .sel(IsJMP));  // open: en
endmodule

module general (
);

  wire clock_1_out, decodeur_instruction_1_isload, decodeur_instruction_1_out_3,
       decodeur_instruction_1_regwrite, Reset_out;
  wire [1:0] controle_de_saut_1_out_3;
  wire [2:0] decodeur_instruction_1_out_4;
  wire [3:0] selecteurreg_1_rd, selecteurreg_1_rs, selecteurreg_1_rt_2, ual_1_flags;
  wire [7:0] adder_1_out, adder_2_out, bancderegistres_1_p8, bancderegistres_1_p9, bit_extender_1_out,
       counter_1_q, multiplexer_1_out, multiplexer_2_out, ual_1_out_5;
  wire [15:0] rom_1_data;

  Button Reset (.out(Reset_out));
  Clock clock_1 (.out(clock_1_out));
  Counter counter_1 (
    .D(multiplexer_2_out), .count(Reset_out), .Q(counter_1_q), .clk(clock_1_out));  // open: load, carry, clr
  Adder adder_1 (.a(counter_1_q), .b(8'h1), .out(adder_1_out));  // open: cin, cout
  ROM #(.dataWidth(16)) rom_1 (.addr(counter_1_q), .data(rom_1_data));  // open: sel
  SelecteurReg selecteurreg_1 (
    .IsJMP(decodeur_instruction_1_out_3), .rd_rs(rom_1_data[11:8]), .rs_rt(rom_1_data[7:4]),
    .rt(rom_1_data[3:0]), .rd(selecteurreg_1_rd), .rs(selecteurreg_1_rs), .rt_2(selecteurreg_1_rt_2));
  Multiplexer #(.width(8)) multiplexer_1 (
    .in0(rom_1_data[7:0]), .in1(ual_1_out_5), .out(multiplexer_1_out), .en(decodeur_instruction_1_isload));  // open: sel
  decodeur_instruction decodeur_instruction_1 (
    .regWrite(decodeur_instruction_1_regwrite), .out_3(decodeur_instruction_1_out_3),
    .isLoad(decodeur_instruction_1_isload), .in_1(rom_1_data[15:12]), .out_4(decodeur_instruction_1_out_4));
  // BancDeRegistres bancderegistres_1: pin names not known; wires that end beside it: multiplexer_1_out, Reset_out, clock_1_out, decodeur_instruction_1_regwrite, selecteurreg_1_rd, selecteurreg_1_rs, selecteurreg_1_rt_2, bancderegistres_1_p8, bancderegistres_1_p9
  assign bit_extender_1_out = {{4{rom_1_data[3]}}, rom_1_data[3:0]};  // Bit_Extender bit_extender_1
  Adder adder_2 (.a(adder_1_out), .b(bit_extender_1_out), .out(adder_2_out));  // open: cin, cout
  UAL ual_1 (
    .in_3(decodeur_instruction_1_out_4), .Flags(ual_1_flags), .out_5(ual_1_out_5), .rs(bancderegistres_1_p8),
    .rt(bancderegistres_1_p9));
  Multiplexer #(.select(2), .width(8)) multiplexer_2 (
    .in0(adder_1_out), .in1({8{1'b1}}), .in2(adder_2_out), .out(multiplexer_2_out),
    .sel(controle_de_saut_1_out_3));  // open: in3, en
  controle_de_saut controle_de_saut_1 (
    .OF_SF_ZF_CF(ual_1_flags), .opcode(rom_1_data[15:12]), .out_3(controle_de_saut_1_out_3));
endmodule
