// Logisim project dlamerde.circ as structural Verilog: 3 circuits, main circuit main
module main (
  input  in_1,
  input  [7:0] in_2,
  input  [7:0] in_3,
  output [7:0] out_4,
  output out_5
);

  BitAdder bitadder_1 ();  // open: in0, out
  Adder adder_1 (.a(in_2), .b(in_3), .out(out_4), .cin(in_1), .cout(out_5));
endmodule

module op (
  input  [7:0] rs,
  input  [7:0] rt,
  input  [2:0] in_3,
  output [3:0] Flags,
  output [7:0] out_5,
  output [7:0] out_6
);

  wire [6:0] multiplexer_1_out;
  wire [7:0] adder_1_out, and_1_out, not_1_out, or_1_out, shifter_1_out, shifter_2_out, subtractor_1_out,
       undriven;

  Adder adder_1 (.a(rs), .b(rt), .out(adder_1_out), .cout(Flags[0]));  // open: cin
  Subtractor subtractor_1 (.a(rs), .b(rt), .out(subtractor_1_out));  // open: bin, bout
  assign or_1_out = rs | rt;  // OR_Gate or_1, 8 bits wide
  assign and_1_out = rs & rt;  // AND_Gate and_1, 8 bits wide
  assign not_1_out = ~rs;  // NOT_Gate not_1, 8 bits wide
  Shifter shifter_1 (.in(rs), .\dist (rt[2:0]), .out(shifter_1_out));
  Shifter #(.shift("lr")) shifter_2 (.in(rs), .\dist (rt[2:0]), .out(shifter_2_out));
  Negator negator_1 (.in(rt), .out(out_5));
  Multiplexer #(.select(3), .width(8)) multiplexer_1 (
    .in0(undriven), .in1(adder_1_out), .in2(subtractor_1_out), .in3(or_1_out), .in4(and_1_out),
    .in5(not_1_out), .in6(shifter_1_out), .in7(shifter_2_out), .out({Flags[2], multiplexer_1_out}), .sel(in_3));  // open: en
  NotExactlyOne xnor_1 (
    .out(Flags[1]), .in0(multiplexer_1_out[0]), .in1(multiplexer_1_out[1]), .in2(multiplexer_1_out[2]),
    .in3(multiplexer_1_out[3]), .in4(multiplexer_1_out[4]), .in5(multiplexer_1_out[5]),
    .in6(multiplexer_1_out[6]), .in7(Flags[2]));
  complement_a_2 complement_a_2_1 (.in_1({Flags[2], multiplexer_1_out}), .out_2(out_6));

  // Notes on the sheet:
  //   convertir les ca2 en normal puis vice verca
  //   halt
endmodule

module a2__unsigned (
  input  [7:0] in_1,
  output [7:0] out_2
);

  wire [7:0] subtractor_1_out, xor_1_out;

  xor xor_1 (xor_1_out[0], 1'b1, in_1[0]);
  xor xor_2 (xor_1_out[1], 1'b1, in_1[1]);
  xor xor_3 (xor_1_out[2], 1'b1, in_1[2]);
  xor xor_4 (xor_1_out[3], 1'b1, in_1[3]);
  xor xor_5 (xor_1_out[4], 1'b1, in_1[4]);
  xor xor_6 (xor_1_out[5], 1'b1, in_1[5]);
  xor xor_7 (xor_1_out[6], 1'b1, in_1[6]);
  xor xor_8 (xor_1_out[7], 1'b1, in_1[7]);
  Subtractor subtractor_1 (.a(xor_1_out), .b(8'h1), .out(subtractor_1_out));  // open: bin, bout
  Multiplexer #(.width(8)) multiplexer_1 (.in0(in_1), .in1(subtractor_1_out), .out(out_2), .sel(in_1[7]));  // open: en
endmodule
