// Logisim project massive_octo_computing_machine.circ as structural Verilog: 3 circuits, main circuit main
module main (
  input  [3:0] in_1,
  input  [3:0] in_2,
  output [1:0] out_3,
  output out_4,
  output out_5,
  output out_6,
  output [2:0] out_7
);

  controle_de_saut controle_de_saut_1 (.CF_ZF_SF_OF(in_1), .opcode(in_2), .out_3(out_3));
  decodeur_instruction decodeur_instruction_1 (
    .regWrite(out_5), .isJump(out_4), .isLoad(out_6), .out_5(out_7), .in_1(in_2));
endmodule

module decodeur_instruction (
  input  [3:0] in_1,
  output regWrite,
  output isJump,
  output isLoad,
  output [2:0] out_5
);

  wire and_1_out, not_1_out, not_2_out, or_1_out, or_2_out;

  and and_1 (and_1_out, in_1[1], ~in_1[0]);  // AND_Gate
  not not_1 (not_1_out, in_1[3]);
  or or_1 (or_1_out, in_1[0], in_1[1], in_1[2]);
  not not_2 (not_2_out, in_1[3]);
  or or_2 (or_2_out, ~in_1[2], ~in_1[1], and_1_out);  // OR_Gate
  and and_2 (regWrite, or_1_out, not_2_out);
  and and_3 (isJump, in_1[3], or_2_out);
  and and_4 (isLoad, in_1[0], in_1[1], in_1[2], in_1[3]);
  and and_5 (out_5[0], in_1[0], not_1_out);
  and and_6 (out_5[1], in_1[1], not_1_out);
  and and_7 (out_5[2], in_1[2], not_1_out);

  // Notes on the sheet:
  //   abcd
  //   isUAL
endmodule

module controle_de_saut (
  input  [3:0] CF_ZF_SF_OF,
  input  [3:0] opcode,
  output [1:0] out_3
);

  wire and_1_out, and_2_out, and_3_out, and_4_out, and_5_out, and_6_out, and_7_out, and_8_out, and_9_out,
       and_10_out, and_11_out, and_12_out, and_13_out, and_14_out, and_15_out, and_16_out, and_17_out,
       and_18_out, and_19_out, and_20_out, and_21_out, and_22_out, and_23_out, or_1_out, or_2_out, or_3_out,
       or_4_out, or_5_out;

  and and_1 (and_1_out, ~opcode[3], ~opcode[2], ~opcode[1], ~opcode[0]);  // AND_Gate
  and and_2 (and_2_out, ~opcode[2], ~opcode[1], ~opcode[0]);  // AND_Gate
  and and_3 (and_3_out, ~opcode[2], ~opcode[1], opcode[0]);  // AND_Gate
  and and_4 (and_4_out, opcode[2], ~opcode[1], opcode[0]);  // AND_Gate
  and and_5 (and_5_out, ~opcode[2], opcode[1], opcode[0]);  // AND_Gate
  and and_6 (and_6_out, opcode[2], ~opcode[1], ~opcode[0]);  // AND_Gate
  and and_7 (and_7_out, opcode[2], ~opcode[1], opcode[0], ~CF_ZF_SF_OF[2]);  // AND_Gate
  and and_8 (and_8_out, opcode[2], opcode[1], ~opcode[0], ~CF_ZF_SF_OF[2]);  // AND_Gate
  and and_9 (and_9_out, CF_ZF_SF_OF[2], and_3_out);
  and and_10 (and_10_out, ~CF_ZF_SF_OF[2], and_4_out);  // AND_Gate
  and and_11 (and_11_out, ~CF_ZF_SF_OF[0], ~CF_ZF_SF_OF[0]);  // AND_Gate
  or or_1 (or_1_out, and_11_out, CF_ZF_SF_OF[2], and_12_out);
  and and_12 (and_12_out, CF_ZF_SF_OF[1], CF_ZF_SF_OF[0]);
  and and_13 (and_13_out, ~CF_ZF_SF_OF[1], CF_ZF_SF_OF[0]);  // AND_Gate
  or or_2 (or_2_out, and_13_out, CF_ZF_SF_OF[2], and_14_out);
  and and_14 (and_14_out, CF_ZF_SF_OF[1], ~CF_ZF_SF_OF[0]);  // AND_Gate
  and and_15 (and_15_out, ~CF_ZF_SF_OF[1], ~CF_ZF_SF_OF[0]);  // AND_Gate
  or or_3 (or_3_out, and_15_out, and_16_out);
  and and_16 (and_16_out, CF_ZF_SF_OF[1], CF_ZF_SF_OF[0]);
  and and_17 (and_17_out, ~CF_ZF_SF_OF[1], CF_ZF_SF_OF[0]);  // AND_Gate
  or or_4 (or_4_out, and_17_out, and_18_out);
  and and_18 (and_18_out, CF_ZF_SF_OF[1], ~CF_ZF_SF_OF[0]);  // AND_Gate
  and and_19 (and_19_out, or_1_out, and_5_out);
  and and_20 (and_20_out, or_2_out, and_6_out);
  and and_21 (and_21_out, or_3_out, and_7_out);
  and and_22 (and_22_out, or_4_out, and_8_out);
  or or_5 (or_5_out, and_2_out, and_9_out, and_10_out, and_19_out, and_20_out, and_21_out, and_22_out);
  and and_23 (and_23_out, or_5_out, opcode[3]);
  not not_1 (out_3[1], and_23_out);
  or or_6 (out_3[0], and_23_out, and_1_out);

  // Notes on the sheet:
  //   ABCD
  //   halt
  //   Saut
endmodule
